# Fritzing sketch led and button connection (saved by Fritzing 0.9.1b)
breadboards: 1

parts:
  Raspberry_Pi_B_rev1 = Raspberry Pi B rev1
  LED1 = smd LED [color="Red (633nm)" package="0805 [SMD]"]
  R1 = Resistor [tolerance=±5% resistance=220 package="0805 [SMD]"]
  S1 = Pushbutton [package="[SMD]"]

nets:
  N1: Raspberry_Pi_B_rev1.3V3, S1.Pin_1, S1.Pin_2
  N2: Raspberry_Pi_B_rev1.GPIO_23, LED1.anode
  N3: Raspberry_Pi_B_rev1.GPIO_24, S1.Pin_3, S1.Pin_4
  N4: Raspberry_Pi_B_rev1.GND, R1.Pin_0
  N5: LED1.cathode, R1.Pin_1
